// Logisim project 4Bit_Design.circ as structural Verilog: 13 circuits, main circuit Four_Bit_ALU
module Four_Bit_ALU (
  input  [3:0] INPUT_A,
  input  [3:0] INPUT_B,
  input  [2:0] OP_CODE,
  output [3:0] Output_Pin,
  output ADD_Over,
  output Sub_Over,
  output [3:0] Mul_Over,
  output Greater,
  output Equal,
  output Less
);

  wire [3:0] adder_1_out, multiplier_1_out, subtractor_1_out;

  Comparator #(.mode("unsigned"), .width(4)) comparator_1 (
    .a(INPUT_A), .b(INPUT_B), .gt(Greater), .eq(Equal), .lt(Less));
  Adder #(.width(4)) adder_1 (.a(INPUT_A), .b(INPUT_B), .out(adder_1_out), .cout(ADD_Over));  // open: cin
  Subtractor #(.width(4)) subtractor_1 (
    .a(INPUT_A), .b(INPUT_B), .out(subtractor_1_out), .bout(Sub_Over));  // open: bin
  Multiplier #(.width(4)) multiplier_1 (
    .a(INPUT_A), .b(INPUT_B), .out(multiplier_1_out), .cout(Mul_Over));  // open: cin
  Multiplexer #(.select(3), .width(4)) multiplexer_1 (
    .in0(adder_1_out), .in1(subtractor_1_out), .in2(multiplier_1_out), .in3({3'b000, Greater}),
    .in4({3'b000, Equal}), .in5({3'b000, Less}), .in6(4'b0000), .in7(4'b0000), .out(Output_Pin), .sel(OP_CODE));

  // Notes on the sheet:
  //   extra work
  //   I have to make sure that all my bits going to
  //   register memory is 4 bit else i have to follow 
  //   ADD 000
  //   SUB 001
  //   MUL 010
  //   COMP 011,100,101
endmodule

module SIX_REGFILE (
  input  [3:0] INPUT_Value,
  input  [2:0] reg_address,
  input  CLK,
  input  RST,
  input  Add_Over,
  input  Sub_Over,
  input  GT,
  input  EQ,
  input  LT,
  input  [3:0] Mul_Over,
  input  Enabler,
  output [3:0] Addition,
  output [3:0] Subtraction,
  output [3:0] Multiplication,
  output [3:0] GREATER,
  output [3:0] EQUAL,
  output [3:0] Less,
  output ADD_OF,
  output S_OF,
  output G_OF,
  output E_OF,
  output L_OF,
  output [7:0] Mul_Final
);

  wire demultiplexer_1_out0, demultiplexer_1_out1, demultiplexer_1_out2, demultiplexer_1_out3,
       demultiplexer_1_out4, demultiplexer_1_out5, demultiplexer_1_out6;
  wire [3:0] multiplexer_1_out;

  Multiplexer #(.select(3), .width(4)) multiplexer_1 (
    .in0(INPUT_Value), .in1(INPUT_Value), .in2(INPUT_Value), .in3(INPUT_Value), .in4(INPUT_Value),
    .in5(INPUT_Value), .in6(4'b0000), .in7(4'b0000), .out(multiplexer_1_out), .sel(reg_address));
  Demultiplexer #(.select(3)) demultiplexer_1 (
    .out0(demultiplexer_1_out0), .out1(demultiplexer_1_out1), .out2(demultiplexer_1_out2),
    .out3(demultiplexer_1_out3), .out4(demultiplexer_1_out4), .out5(demultiplexer_1_out5),
    .out6(demultiplexer_1_out6), .out7(demultiplexer_1_out6), .in(Enabler), .sel(reg_address));
  Register #(.width(4)) reg_01 (.D(multiplexer_1_out), .en(demultiplexer_1_out0), .clk(CLK), .Q(Addition), .clr(RST));
  Register #(.width(4)) reg_02 (
    .D(multiplexer_1_out), .en(demultiplexer_1_out1), .clk(CLK), .Q(Subtraction), .clr(RST));
  Register #(.width(4)) reg_03 (
    .D(multiplexer_1_out), .en(demultiplexer_1_out2), .clk(CLK), .Q(Mul_Final[3:0]), .clr(RST));
  Register #(.width(4)) reg_04 (.D(multiplexer_1_out), .en(demultiplexer_1_out3), .clk(CLK), .Q(GREATER), .clr(RST));
  Register #(.width(4)) reg_05 (.D(multiplexer_1_out), .en(demultiplexer_1_out4), .clk(CLK), .Q(EQUAL), .clr(RST));
  Register #(.width(4)) reg_06 (.D(multiplexer_1_out), .en(demultiplexer_1_out5), .clk(CLK), .Q(Less), .clr(RST));
  Register #(.width(1)) ADD (.D(Add_Over), .en(demultiplexer_1_out0), .clk(CLK), .Q(ADD_OF), .clr(RST));
  Register #(.width(1)) SUB (.D(Sub_Over), .en(demultiplexer_1_out1), .clk(CLK), .Q(S_OF), .clr(RST));
  Register #(.width(1)) G (.D(GT), .en(demultiplexer_1_out3), .clk(CLK), .Q(G_OF), .clr(RST));
  Register #(.width(1)) E (.D(EQ), .en(demultiplexer_1_out4), .clk(CLK), .Q(E_OF), .clr(RST));
  Register #(.width(1)) L (.D(LT), .en(demultiplexer_1_out5), .clk(CLK), .Q(L_OF), .clr(RST));
  Register #(.width(4)) MUL (.D(Mul_Over), .en(demultiplexer_1_out2), .clk(CLK), .Q(Mul_Final[7:4]), .clr(RST));

  assign Multiplication = Mul_Final[3:0];
  // also tied to GND on the sheet: demultiplexer_1_out6

  // Notes on the sheet:
  //   Made By Faizan
  //   I am making chages to store overflows in extra registers
  //   Here I Only Have To Give Only The Mux Address And The Value Will Be Automatically Fetched
endmodule

module Control_Unit (
  input  [2:0] Program_Counter,
  output Reset_PIN,
  output [3:0] State_Check
);

  wire not_1_out;

  not not_1 (not_1_out, Program_Counter[0]);
  and and_1 (Reset_PIN, not_1_out, Program_Counter[1], Program_Counter[2]);

  assign State_Check = {1'b0, Program_Counter};
endmodule

module State_Control (
  input  CLK,
  output Reset_Pin,
  output Reg_File,
  output RE_DataMemory,
  output WE_A,
  output WE_B,
  output Selection_AB,
  output RE_Instruction,
  output [3:0] State_Number
);

  wire A_out, B_out, not_1_out, not_2_out, not_3_out, not_4_out, not_5_out, not_6_out, not_7_out, not_8_out,
       not_9_out, not_10_out, not_11_out, not_12_out, not_13_out, not_14_out;

  Counter #(.max('h6), .width(3)) Sub_Counter (
    .clk(CLK), .Q(State_Number[2:0]));  // open: clr, load, up, count, D, carry
  not not_1 (not_1_out, State_Number[0]);
  not not_2 (not_2_out, State_Number[1]);
  not not_3 (not_3_out, State_Number[2]);
  not not_4 (not_4_out, State_Number[1]);
  not not_5 (not_5_out, State_Number[2]);
  not not_6 (not_6_out, State_Number[0]);
  not not_7 (not_7_out, State_Number[2]);
  not not_8 (not_8_out, State_Number[0]);
  not not_9 (not_9_out, State_Number[1]);
  not not_10 (not_10_out, State_Number[2]);
  not not_11 (not_11_out, State_Number[0]);
  not not_12 (not_12_out, State_Number[1]);
  not not_13 (not_13_out, State_Number[1]);
  not not_14 (not_14_out, State_Number[2]);
  and Reset (Reset_Pin, not_1_out, not_2_out, not_3_out);
  and and_1 (Reg_File, State_Number[0], not_4_out, State_Number[2]);
  and RE2 (RE_DataMemory, State_Number[0], not_5_out);
  and WEa (WE_A, not_6_out, State_Number[1], not_7_out);
  and WEb (WE_B, not_8_out, not_9_out, State_Number[2]);
  and A (A_out, State_Number[0], State_Number[1], not_10_out);
  and B (B_out, not_11_out, not_12_out, State_Number[2]);
  and RE1 (RE_Instruction, State_Number[0], not_13_out, not_14_out);
  or or_1 (Selection_AB, A_out, B_out);

  assign State_Number[3] = 1'b0;

  // Notes on the sheet:
  //   s2
  //   s0
  //   s1
endmodule

module MY_CPU (
  input  Stop_Circ,
  input  WRITE_DM,
  input  [2:0] in_3,
  input  [2:0] in_4
);

  wire A, and_1_out, and_2_out, B, C, clock_1_out, clock_2_out, control_unit_1_reset_pin, D, E,
       four_bit_alu_1_add_over, four_bit_alu_1_equal, four_bit_alu_1_greater, four_bit_alu_1_less,
       four_bit_alu_1_sub_over, n7_segment_display_1_p1, n7_segment_display_2_p1, n7_segment_display_3_p1,
       n7_segment_display_4_p1, n7_segment_display_5_p1, n7_segment_display_6_p1, n7_segment_display_7_p1,
       n7_segment_display_8_p1, n7_segment_display_9_p1, n7_segment_display_10_p1, n7_segment_display_11_p1,
       not_1_out, not_2_out, state_control_1_re_datamemory, state_control_1_re_instruction,
       state_control_1_reg_file, state_control_1_reset_pin, state_control_1_selection_ab,
       state_control_1_we_a, state_control_1_we_b;
  wire [2:0] multiplexer_1_out, Program_Counter_q, selector_of_mem_1_addr;
  wire [3:0] A_q, ANS, B_q, binary_to_bcd_converter_1_p1, binary_to_bcd_converter_2_p2, Data_Memory_dout,
       four_bit_alu_1_mul_over, four_bit_alu_1_output_pin, twelve_regfile_1_addition, twelve_regfile_1_equal,
       twelve_regfile_1_greater, twelve_regfile_1_less, twelve_regfile_1_multiplication,
       twelve_regfile_1_subtraction, undriven;
  wire [4:0] ADD;
  wire [7:0] MUL;
  wire [8:0] Instruction_Memory_dout;

  Clock clock_1 (.out(clock_1_out));
  not not_1 (not_1_out, Stop_Circ);
  Clock #(.lowDuration(13)) clock_2 (.out(clock_2_out));
  not not_2 (not_2_out, Stop_Circ);
  and and_1 (and_1_out, clock_1_out, not_1_out);
  and and_2 (and_2_out, clock_2_out, not_2_out);
  LED led_1 (.in(A));
  LED led_2 (.in(B));
  LED led_3 (.in(C));
  LED led_4 (.in(D));
  LED led_5 (.in(E));
  // _7_Segment_Display 7_segment_display_1: pin names not known; wires that end beside it: n7_segment_display_1_p1, n7_segment_display_1_p1
  // _7_Segment_Display 7_segment_display_2: pin names not known; wires that end beside it: n7_segment_display_2_p1, n7_segment_display_2_p1
  // BCD_to_7_Segment_decoder bcd_to_7_segment_decoder_1: pin names not known
  // BCD_to_7_Segment_decoder bcd_to_7_segment_decoder_2: pin names not known
  // Binary_to_BCD_converter #(.binvalue(4)) binary_to_bcd_converter_1: pin names not known; wires that end beside it: binary_to_bcd_converter_1_p1
  // _7_Segment_Display 7_segment_display_3: pin names not known; wires that end beside it: n7_segment_display_3_p1, n7_segment_display_3_p1
  // _7_Segment_Display 7_segment_display_4: pin names not known; wires that end beside it: n7_segment_display_4_p1, n7_segment_display_4_p1
  // BCD_to_7_Segment_decoder bcd_to_7_segment_decoder_3: pin names not known
  // BCD_to_7_Segment_decoder bcd_to_7_segment_decoder_4: pin names not known
  // Binary_to_BCD_converter #(.binvalue(4)) binary_to_bcd_converter_2: pin names not known; wires that end beside it: clock_2_out, binary_to_bcd_converter_2_p2
  State_Control state_control_1 (
    .CLK(and_1_out), .Reset_Pin(state_control_1_reset_pin), .Reg_File(state_control_1_reg_file),
    .RE_DataMemory(state_control_1_re_datamemory), .WE_A(state_control_1_we_a), .WE_B(state_control_1_we_b),
    .Selection_AB(state_control_1_selection_ab), .RE_Instruction(state_control_1_re_instruction),
    .State_Number(binary_to_bcd_converter_1_p1));
  Control_Unit control_unit_1 (
    .Program_Counter(Program_Counter_q), .Reset_PIN(control_unit_1_reset_pin),
    .State_Check(binary_to_bcd_converter_2_p2));
  Counter #(.max('h6), .width(3)) Program_Counter (
    .clk(and_2_out), .Q(Program_Counter_q));  // open: clr, load, up, count, D, carry
  RAM #(.addrWidth(3), .dataWidth(9)) Instruction_Memory (
    .addr(Program_Counter_q), .oe(state_control_1_re_instruction), .clk(and_1_out),
    .dout(Instruction_Memory_dout));  // open: we, din
  Register #(.width(4)) u_A (
    .D(Data_Memory_dout), .en(state_control_1_we_a), .clk(and_1_out), .Q(A_q), .clr(state_control_1_reset_pin));
  Register #(.width(4)) u_B (
    .D(Data_Memory_dout), .en(state_control_1_we_b), .clk(and_1_out), .Q(B_q), .clr(state_control_1_reset_pin));
  // _7_Segment_Display 7_segment_display_5: pin names not known; wires that end beside it: n7_segment_display_5_p1, n7_segment_display_5_p1
  // BCD_to_7_Segment_decoder bcd_to_7_segment_decoder_5: pin names not known
  // _7_Segment_Display 7_segment_display_6: pin names not known; wires that end beside it: n7_segment_display_6_p1, n7_segment_display_6_p1
  // BCD_to_7_Segment_decoder bcd_to_7_segment_decoder_6: pin names not known
  // Binary_to_BCD_converter #(.binvalue(5)) binary_to_bcd_converter_3: pin names not known; wires that end beside it: ADD, and_1_out
  Multiplexer #(.width(3)) multiplexer_1 (
    .in0(Instruction_Memory_dout[8:6]), .in1(Instruction_Memory_dout[5:3]), .out(multiplexer_1_out),
    .sel(state_control_1_selection_ab));
  selector_of_mem selector_of_mem_1 (
    .Mux_Inp(multiplexer_1_out), .ADD_OF_RAM(in_3), .EN_REG(state_control_1_reg_file),
    .ADDR(selector_of_mem_1_addr));
  RAM #(.addrWidth(3), .dataWidth(4)) Data_Memory (
    .addr(selector_of_mem_1_addr), .we(state_control_1_reg_file), .oe(state_control_1_re_datamemory),
    .clk(and_1_out), .din(four_bit_alu_1_output_pin), .dout(Data_Memory_dout));
  Four_Bit_ALU four_bit_alu_1 (
    .INPUT_A(A_q), .INPUT_B(B_q), .OP_CODE(Instruction_Memory_dout[2:0]),
    .Output_Pin(four_bit_alu_1_output_pin), .ADD_Over(four_bit_alu_1_add_over),
    .Sub_Over(four_bit_alu_1_sub_over), .Mul_Over(four_bit_alu_1_mul_over), .Greater(four_bit_alu_1_greater),
    .Equal(four_bit_alu_1_equal), .Less(four_bit_alu_1_less));
  // _7_Segment_Display 7_segment_display_7: pin names not known; wires that end beside it: n7_segment_display_7_p1, n7_segment_display_7_p1
  // BCD_to_7_Segment_decoder bcd_to_7_segment_decoder_7: pin names not known
  // Binary_to_BCD_converter #(.binvalue(4)) binary_to_bcd_converter_4: pin names not known; wires that end beside it: ANS
  // _7_Segment_Display 7_segment_display_8: pin names not known; wires that end beside it: n7_segment_display_8_p1, n7_segment_display_8_p1
  // BCD_to_7_Segment_decoder bcd_to_7_segment_decoder_8: pin names not known
  // _7_Segment_Display 7_segment_display_9: pin names not known; wires that end beside it: n7_segment_display_9_p1, n7_segment_display_9_p1
  // BCD_to_7_Segment_decoder bcd_to_7_segment_decoder_9: pin names not known
  // Binary_to_BCD_converter #(.binvalue(8)) binary_to_bcd_converter_5: pin names not known; wires that end beside it: MUL
  TWELVE_REGFILE twelve_regfile_1 (
    .INPUT_Value(four_bit_alu_1_output_pin), .reg_address(Program_Counter_q), .CLK(and_1_out),
    .Add_Over(four_bit_alu_1_add_over), .Sub_Over(four_bit_alu_1_sub_over),
    .Mul_Over(four_bit_alu_1_mul_over), .GT(four_bit_alu_1_greater), .EQ(four_bit_alu_1_equal),
    .LT(four_bit_alu_1_less), .Enabler(state_control_1_reg_file), .Addition(twelve_regfile_1_addition),
    .Subtraction(twelve_regfile_1_subtraction), .Multiplication(twelve_regfile_1_multiplication),
    .GREATER(twelve_regfile_1_greater), .EQUAL(twelve_regfile_1_equal), .Less(twelve_regfile_1_less),
    .ADD_OF(A), .S_OF(B), .G_OF(C), .E_OF(D), .L_OF(E), .ADD_FINAL(ADD), .Mul_Final(MUL));  // open: RST
  // _7_Segment_Display 7_segment_display_10: pin names not known; wires that end beside it: n7_segment_display_10_p1, n7_segment_display_10_p1
  // BCD_to_7_Segment_decoder bcd_to_7_segment_decoder_10: pin names not known
  Multiplexer #(.select(3), .width(4)) multiplexer_2 (
    .in0(twelve_regfile_1_addition), .in1(twelve_regfile_1_subtraction),
    .in2(twelve_regfile_1_multiplication), .in3(twelve_regfile_1_greater), .in4(twelve_regfile_1_equal),
    .in5(twelve_regfile_1_less), .in6(undriven), .in7(undriven), .out(ANS), .sel(in_4));
  // _7_Segment_Display 7_segment_display_11: pin names not known; wires that end beside it: n7_segment_display_11_p1, n7_segment_display_11_p1
  // BCD_to_7_Segment_decoder bcd_to_7_segment_decoder_11: pin names not known

  // Other names for the same wires on the sheet: RAM_ADD[2:0] = in_3; STOP = Stop_Circ; W_DM = WRITE_DM

  // Notes on the sheet:
  //   If Overflows occur this led's will be light up
  //   Addition Result
  //   Results Stored in Register File
  //   Multiplication Result
endmodule

module TWELVE_REGFILE (
  input  [3:0] INPUT_Value,
  input  [2:0] reg_address,
  input  CLK,
  input  RST,
  input  Add_Over,
  input  Sub_Over,
  input  [3:0] Mul_Over,
  input  GT,
  input  EQ,
  input  LT,
  input  Enabler,
  output [3:0] Addition,
  output [3:0] Subtraction,
  output [3:0] Multiplication,
  output [3:0] GREATER,
  output [3:0] EQUAL,
  output [3:0] Less,
  output ADD_OF,
  output S_OF,
  output G_OF,
  output E_OF,
  output L_OF,
  output [4:0] ADD_FINAL,
  output [7:0] Mul_Final
);

  wire demultiplexer_1_out0, demultiplexer_1_out1, demultiplexer_1_out2, demultiplexer_1_out3,
       demultiplexer_1_out4, demultiplexer_1_out5, demultiplexer_1_out6;
  wire [3:0] multiplexer_1_out;

  Multiplexer #(.select(3), .width(4)) multiplexer_1 (
    .in0(INPUT_Value), .in1(INPUT_Value), .in2(INPUT_Value), .in3(INPUT_Value), .in4(INPUT_Value),
    .in5(INPUT_Value), .in6(4'b0000), .in7(4'b0000), .out(multiplexer_1_out), .sel(reg_address));
  Demultiplexer #(.select(3)) demultiplexer_1 (
    .out0(demultiplexer_1_out0), .out1(demultiplexer_1_out1), .out2(demultiplexer_1_out2),
    .out3(demultiplexer_1_out3), .out4(demultiplexer_1_out4), .out5(demultiplexer_1_out5),
    .out6(demultiplexer_1_out6), .out7(demultiplexer_1_out6), .in(Enabler), .sel(reg_address));
  Register #(.width(4)) reg_01 (
    .D(multiplexer_1_out), .en(demultiplexer_1_out0), .clk(CLK), .Q(ADD_FINAL[3:0]), .clr(RST));
  Register #(.width(4)) reg_02 (
    .D(multiplexer_1_out), .en(demultiplexer_1_out1), .clk(CLK), .Q(Subtraction), .clr(RST));
  Register #(.width(4)) reg_03 (
    .D(multiplexer_1_out), .en(demultiplexer_1_out2), .clk(CLK), .Q(Mul_Final[3:0]), .clr(RST));
  Register #(.width(4)) reg_04 (.D(multiplexer_1_out), .en(demultiplexer_1_out3), .clk(CLK), .Q(GREATER), .clr(RST));
  Register #(.width(4)) reg_05 (.D(multiplexer_1_out), .en(demultiplexer_1_out4), .clk(CLK), .Q(EQUAL), .clr(RST));
  Register #(.width(4)) reg_06 (.D(multiplexer_1_out), .en(demultiplexer_1_out5), .clk(CLK), .Q(Less), .clr(RST));
  Register #(.width(1)) ADD (.D(Add_Over), .en(demultiplexer_1_out0), .clk(CLK), .Q(ADD_FINAL[4]), .clr(RST));
  Register #(.width(1)) SUB (.D(Sub_Over), .en(demultiplexer_1_out1), .clk(CLK), .Q(S_OF), .clr(RST));
  Register #(.width(1)) G (.D(GT), .en(demultiplexer_1_out3), .clk(CLK), .Q(G_OF), .clr(RST));
  Register #(.width(1)) E (.D(EQ), .en(demultiplexer_1_out4), .clk(CLK), .Q(E_OF), .clr(RST));
  Register #(.width(1)) L (.D(LT), .en(demultiplexer_1_out5), .clk(CLK), .Q(L_OF), .clr(RST));
  Register #(.width(4)) MUL (.D(Mul_Over), .en(demultiplexer_1_out2), .clk(CLK), .Q(Mul_Final[7:4]), .clr(RST));

  assign ADD_OF = ADD_FINAL[4];
  assign Addition = ADD_FINAL[3:0];
  assign Multiplication = Mul_Final[3:0];
  // also tied to GND on the sheet: demultiplexer_1_out6

  // Notes on the sheet:
  //   I am making chages to store overflows in extra registers
  //   Here I Only Have To Give Only The Mux Address And The Value Will Be Automatically Fetched
endmodule

module ALU (
  input  [3:0] VALUES,
  input  EN_A,
  input  EN_B,
  input  RST_REG,
  input  [2:0] OP_CODE,
  output [3:0] Output_Pin,
  output ADD_Over,
  output Sub_Over,
  output [3:0] Mul_Over,
  output Greater,
  output Equal,
  output Less
);

  wire clock_1_out;
  wire [3:0] A_q, adder_1_out, B_q, multiplier_1_out, subtractor_1_out;

  Clock clock_1 (.out(clock_1_out));
  Register #(.width(4)) A (.D(VALUES), .en(EN_A), .clk(clock_1_out), .Q(A_q), .clr(RST_REG));
  Register #(.width(4)) B (.D(VALUES), .en(EN_B), .clk(clock_1_out), .Q(B_q), .clr(RST_REG));
  Comparator #(.mode("unsigned"), .width(4)) comparator_1 (.a(A_q), .b(B_q), .gt(Greater), .eq(Equal), .lt(Less));
  Adder #(.width(4)) adder_1 (.a(A_q), .b(B_q), .out(adder_1_out), .cout(ADD_Over));  // open: cin
  Subtractor #(.width(4)) subtractor_1 (.a(A_q), .b(B_q), .out(subtractor_1_out), .bout(Sub_Over));  // open: bin
  Multiplier #(.width(4)) multiplier_1 (.a(A_q), .b(B_q), .out(multiplier_1_out), .cout(Mul_Over));  // open: cin
  Multiplexer #(.select(3), .width(4)) multiplexer_1 (
    .in0(adder_1_out), .in1(subtractor_1_out), .in2(multiplier_1_out), .in3({3'b000, Greater}),
    .in4({3'b000, Equal}), .in5({3'b000, Less}), .in6(4'b0000), .in7(4'b0000), .out(Output_Pin), .sel(OP_CODE));

  // Notes on the sheet:
  //   extra work
  //   I have to make sure that all my bits going to
  //   register memory is 4 bit else i have to follow 
  //   SUB 001
  //   MUL 010
  //   COMP 011,100,101
  //   ADD 000 and 111 If overflows
endmodule

module Block_CPU (
  input  [2:0] in_1
);

  wire A, alu_1_add_over, alu_1_equal, alu_1_greater, alu_1_less, alu_1_sub_over, B, C,
       control_unit_block_1_re_dm, control_unit_block_1_re_im, control_unit_block_1_reg_en,
       control_unit_block_1_rst, control_unit_block_1_rst_reg, control_unit_block_1_selector,
       control_unit_block_1_we_a, control_unit_block_1_we_b, D, E, n7_segment_display_1_p1,
       n7_segment_display_2_p1, n7_segment_display_3_p1, n7_segment_display_4_p1, n7_segment_display_5_p1,
       n7_segment_display_6_p1, n7_segment_display_7_p1, n7_segment_display_8_p1, n7_segment_display_9_p1,
       n7_segment_display_10_p1, n7_segment_display_11_p1;
  wire [2:0] control_unit_block_1_op_code, instruction_mem_1_add_a, instruction_mem_1_add_b,
       instruction_mem_1_op_code;
  wire [3:0] alu_1_mul_over, alu_1_output_pin, ANS, binary_to_bcd_converter_4_p2, data_mem_1_values, PC, SC,
       twelve_regfile_1_addition, twelve_regfile_1_equal, twelve_regfile_1_greater, twelve_regfile_1_less,
       twelve_regfile_1_multiplication, undriven;
  wire [4:0] ADD;
  wire [7:0] MUL;

  CONTROL_UNIT_BLOCK control_unit_block_1 (
    .RST(control_unit_block_1_rst), .REG_EN(control_unit_block_1_reg_en), .RE_DM(control_unit_block_1_re_dm),
    .WE_A(control_unit_block_1_we_a), .WE_B(control_unit_block_1_we_b),
    .SELECTOR(control_unit_block_1_selector), .RE_IM(control_unit_block_1_re_im), .STATE_SC(SC),
    .RST_REG(control_unit_block_1_rst_reg), .STATE_PC(PC), .OP_CODE(control_unit_block_1_op_code));
  LED led_1 (.in(A));
  LED led_2 (.in(B));
  LED led_3 (.in(C));
  LED led_4 (.in(D));
  LED led_5 (.in(E));
  INSTRUCTION_MEM instruction_mem_1 (
    .ADDRESS(control_unit_block_1_op_code), .RE_IM(control_unit_block_1_re_im),
    .ADD_A(instruction_mem_1_add_a), .ADD_B(instruction_mem_1_add_b), .OP_CODE(instruction_mem_1_op_code));
  DATA_MEM data_mem_1 (
    .ADD_A(instruction_mem_1_add_a), .ADD_B(instruction_mem_1_add_b),
    .SELECTOR(control_unit_block_1_selector), .RE_DM(control_unit_block_1_re_dm), .VALUES(data_mem_1_values));
  // _7_Segment_Display 7_segment_display_1: pin names not known; wires that end beside it: n7_segment_display_1_p1, n7_segment_display_1_p1
  // BCD_to_7_Segment_decoder bcd_to_7_segment_decoder_1: pin names not known
  ALU alu_1 (
    .VALUES(data_mem_1_values), .EN_A(control_unit_block_1_we_b), .EN_B(control_unit_block_1_we_a),
    .RST_REG(control_unit_block_1_rst_reg), .OP_CODE(instruction_mem_1_op_code),
    .Output_Pin(alu_1_output_pin), .ADD_Over(alu_1_add_over), .Sub_Over(alu_1_sub_over),
    .Mul_Over(alu_1_mul_over), .Greater(alu_1_greater), .Equal(alu_1_equal), .Less(alu_1_less));
  // _7_Segment_Display 7_segment_display_2: pin names not known; wires that end beside it: n7_segment_display_2_p1, n7_segment_display_2_p1
  // BCD_to_7_Segment_decoder bcd_to_7_segment_decoder_2: pin names not known
  // Binary_to_BCD_converter #(.binvalue(5)) binary_to_bcd_converter_1: pin names not known; wires that end beside it: ADD
  // _7_Segment_Display 7_segment_display_3: pin names not known; wires that end beside it: n7_segment_display_3_p1, n7_segment_display_3_p1
  // BCD_to_7_Segment_decoder bcd_to_7_segment_decoder_3: pin names not known
  // Binary_to_BCD_converter #(.binvalue(4)) binary_to_bcd_converter_2: pin names not known; wires that end beside it: SC
  // _7_Segment_Display 7_segment_display_4: pin names not known; wires that end beside it: n7_segment_display_4_p1, n7_segment_display_4_p1
  // BCD_to_7_Segment_decoder bcd_to_7_segment_decoder_4: pin names not known
  // _7_Segment_Display 7_segment_display_5: pin names not known; wires that end beside it: n7_segment_display_5_p1, n7_segment_display_5_p1
  // BCD_to_7_Segment_decoder bcd_to_7_segment_decoder_5: pin names not known
  // Binary_to_BCD_converter #(.binvalue(4)) binary_to_bcd_converter_3: pin names not known; wires that end beside it: ANS
  // _7_Segment_Display 7_segment_display_6: pin names not known; wires that end beside it: n7_segment_display_6_p1, n7_segment_display_6_p1
  // _7_Segment_Display 7_segment_display_7: pin names not known; wires that end beside it: n7_segment_display_7_p1, n7_segment_display_7_p1
  // BCD_to_7_Segment_decoder bcd_to_7_segment_decoder_6: pin names not known
  // BCD_to_7_Segment_decoder bcd_to_7_segment_decoder_7: pin names not known
  // Binary_to_BCD_converter #(.binvalue(4)) binary_to_bcd_converter_4: pin names not known; wires that end beside it: PC, binary_to_bcd_converter_4_p2
  TWELVE_REGFILE twelve_regfile_1 (
    .INPUT_Value(alu_1_output_pin), .reg_address(control_unit_block_1_op_code),
    .RST(control_unit_block_1_rst), .Add_Over(alu_1_add_over), .Sub_Over(alu_1_sub_over),
    .Mul_Over(alu_1_mul_over), .GT(alu_1_greater), .EQ(alu_1_equal), .LT(alu_1_less),
    .Enabler(control_unit_block_1_reg_en), .Addition(twelve_regfile_1_addition),
    .Multiplication(twelve_regfile_1_multiplication), .GREATER(twelve_regfile_1_greater),
    .EQUAL(twelve_regfile_1_equal), .Less(twelve_regfile_1_less), .ADD_OF(A), .S_OF(B), .G_OF(C), .E_OF(D),
    .L_OF(E), .ADD_FINAL(ADD), .Mul_Final(MUL));  // open: CLK, Subtraction
  // _7_Segment_Display 7_segment_display_8: pin names not known; wires that end beside it: n7_segment_display_8_p1, n7_segment_display_8_p1
  // BCD_to_7_Segment_decoder bcd_to_7_segment_decoder_8: pin names not known
  Multiplexer #(.select(3), .width(4)) multiplexer_1 (
    .in0(twelve_regfile_1_addition), .in1(binary_to_bcd_converter_4_p2),
    .in2(twelve_regfile_1_multiplication), .in3(twelve_regfile_1_greater), .in4(twelve_regfile_1_equal),
    .in5(twelve_regfile_1_less), .in6(undriven), .in7(undriven), .out(ANS), .sel(in_1));
  // _7_Segment_Display 7_segment_display_9: pin names not known; wires that end beside it: n7_segment_display_9_p1, n7_segment_display_9_p1
  // BCD_to_7_Segment_decoder bcd_to_7_segment_decoder_9: pin names not known
  // Binary_to_BCD_converter #(.binvalue(8)) binary_to_bcd_converter_5: pin names not known; wires that end beside it: MUL
  // _7_Segment_Display 7_segment_display_10: pin names not known; wires that end beside it: n7_segment_display_10_p1, n7_segment_display_10_p1
  // BCD_to_7_Segment_decoder bcd_to_7_segment_decoder_10: pin names not known
  // _7_Segment_Display 7_segment_display_11: pin names not known; wires that end beside it: n7_segment_display_11_p1, n7_segment_display_11_p1
  // BCD_to_7_Segment_decoder bcd_to_7_segment_decoder_11: pin names not known

  // Other names for the same wires on the sheet: ADDRESS[2:0] = in_1

  // Notes on the sheet:
  //   If Overflows occur this led's will be light up
  //   Addition Result
  //   Sub Counter State
  //   Program Counter
  //   Results Stored in Register File
  //   Multiplication Result
endmodule

module CONTROL_UNIT_BLOCK (
  output RST,
  output REG_EN,
  output RE_DM,
  output WE_A,
  output WE_B,
  output SELECTOR,
  output RE_IM,
  output [3:0] STATE_SC,
  output RST_REG,
  output [3:0] STATE_PC,
  output [2:0] OP_CODE
);

  wire clock_1_out, clock_2_out;

  Counter #(.max('h6), .width(3)) Program_Counter (
    .clk(clock_1_out), .Q(OP_CODE));  // open: clr, load, up, count, D, carry
  Clock #(.lowDuration(13)) clock_1 (.out(clock_1_out));
  Clock clock_2 (.out(clock_2_out));
  State_Control state_control_1 (
    .CLK(clock_2_out), .Reset_Pin(RST), .Reg_File(REG_EN), .RE_DataMemory(RE_DM), .WE_A(WE_A), .WE_B(WE_B),
    .Selection_AB(SELECTOR), .RE_Instruction(RE_IM), .State_Number(STATE_SC));
  Control_Unit control_unit_1 (.Program_Counter(OP_CODE), .Reset_PIN(RST_REG), .State_Check(STATE_PC));
endmodule

module INSTRUCTION_MEM (
  input  [2:0] ADDRESS,
  input  RE_IM,
  output [2:0] ADD_A,
  output [2:0] ADD_B,
  output [2:0] OP_CODE
);

  wire clock_1_out;

  RAM #(.addrWidth(3), .dataWidth(9)) Instruction_Memory (
    .addr(ADDRESS), .oe(RE_IM), .clk(clock_1_out), .dout({ADD_A, ADD_B, OP_CODE}));  // open: we, din
  Clock clock_1 (.out(clock_1_out));
endmodule

module DATA_MEM (
  input  [2:0] ADD_A,
  input  [2:0] ADD_B,
  input  SELECTOR,
  input  RE_DM,
  output [3:0] VALUES
);

  wire clock_1_out;
  wire [2:0] multiplexer_1_out;

  Multiplexer #(.width(3)) multiplexer_1 (.in0(ADD_A), .in1(ADD_B), .out(multiplexer_1_out), .sel(SELECTOR));
  Clock clock_1 (.out(clock_1_out));
  RAM #(.addrWidth(3), .dataWidth(4)) Data_Memory (
    .addr(multiplexer_1_out), .oe(RE_DM), .clk(clock_1_out), .dout(VALUES));  // open: we, din
endmodule

module REG_FILE_BLOCK (
  input  [3:0] INPUT_Value,
  input  [2:0] reg_address,
  input  RST,
  input  Add_Over,
  input  Sub_Over,
  input  [3:0] Mul_Over,
  input  GT,
  input  EQ,
  input  LT,
  input  Enabler,
  output [3:0] Addition,
  output [3:0] Subtraction,
  output [3:0] Multiplication,
  output [3:0] GREATER,
  output [3:0] EQUAL,
  output [3:0] Less,
  output ADD_OF,
  output S_OF,
  output G_OF,
  output E_OF,
  output L_OF,
  output [4:0] ADD_FINAL,
  output [7:0] Mul_Final
);

  wire clock_1_out, demultiplexer_1_out0, demultiplexer_1_out1, demultiplexer_1_out2, demultiplexer_1_out3,
       demultiplexer_1_out4, demultiplexer_1_out5, demultiplexer_1_out6;
  wire [3:0] multiplexer_1_out;

  Clock clock_1 (.out(clock_1_out));
  Multiplexer #(.select(3), .width(4)) multiplexer_1 (
    .in0(INPUT_Value), .in1(INPUT_Value), .in2(INPUT_Value), .in3(INPUT_Value), .in4(INPUT_Value),
    .in5(INPUT_Value), .in6(4'b0000), .in7(4'b0000), .out(multiplexer_1_out), .sel(reg_address));
  Demultiplexer #(.select(3)) demultiplexer_1 (
    .out0(demultiplexer_1_out0), .out1(demultiplexer_1_out1), .out2(demultiplexer_1_out2),
    .out3(demultiplexer_1_out3), .out4(demultiplexer_1_out4), .out5(demultiplexer_1_out5),
    .out6(demultiplexer_1_out6), .out7(demultiplexer_1_out6), .in(Enabler), .sel(reg_address));
  Register #(.width(4)) reg_01 (
    .D(multiplexer_1_out), .en(demultiplexer_1_out0), .clk(clock_1_out), .Q(ADD_FINAL[3:0]), .clr(RST));
  Register #(.width(4)) reg_02 (
    .D(multiplexer_1_out), .en(demultiplexer_1_out1), .clk(clock_1_out), .Q(Subtraction), .clr(RST));
  Register #(.width(4)) reg_03 (
    .D(multiplexer_1_out), .en(demultiplexer_1_out2), .clk(clock_1_out), .Q(Mul_Final[3:0]), .clr(RST));
  Register #(.width(4)) reg_04 (
    .D(multiplexer_1_out), .en(demultiplexer_1_out3), .clk(clock_1_out), .Q(GREATER), .clr(RST));
  Register #(.width(4)) reg_05 (
    .D(multiplexer_1_out), .en(demultiplexer_1_out4), .clk(clock_1_out), .Q(EQUAL), .clr(RST));
  Register #(.width(4)) reg_06 (
    .D(multiplexer_1_out), .en(demultiplexer_1_out5), .clk(clock_1_out), .Q(Less), .clr(RST));
  Register #(.width(1)) ADD (.D(Add_Over), .en(demultiplexer_1_out0), .clk(clock_1_out), .Q(ADD_FINAL[4]), .clr(RST));
  Register #(.width(1)) SUB (.D(Sub_Over), .en(demultiplexer_1_out1), .clk(clock_1_out), .Q(S_OF), .clr(RST));
  Register #(.width(1)) G (.D(GT), .en(demultiplexer_1_out3), .clk(clock_1_out), .Q(G_OF), .clr(RST));
  Register #(.width(1)) E (.D(EQ), .en(demultiplexer_1_out4), .clk(clock_1_out), .Q(E_OF), .clr(RST));
  Register #(.width(1)) L (.D(LT), .en(demultiplexer_1_out5), .clk(clock_1_out), .Q(L_OF), .clr(RST));
  Register #(.width(4)) MUL (.D(Mul_Over), .en(demultiplexer_1_out2), .clk(clock_1_out), .Q(Mul_Final[7:4]), .clr(RST));

  assign ADD_OF = ADD_FINAL[4];
  assign Addition = ADD_FINAL[3:0];
  assign Multiplication = Mul_Final[3:0];
  // also tied to GND on the sheet: demultiplexer_1_out6

  // Notes on the sheet:
  //   I am making chages to store overflows in extra registers
  //   Here I Only Have To Give Only The Mux Address And The Value Will Be Automatically Fetched
endmodule

module selector_of_mem (
  input  [2:0] Mux_Inp,
  input  [2:0] ADD_OF_RAM,
  input  EN_REG,
  output [2:0] ADDR
);

  Multiplexer #(.width(3)) multiplexer_1 (.in0(Mux_Inp), .in1(ADD_OF_RAM), .out(ADDR), .sel(EN_REG));
endmodule
